// Logisim project BINARY ARCADE FINAL.circ as structural Verilog: 10 circuits, main circuit main
module main (
  input  in_1,
  input  in_2,
  input  in_3,
  input  in_4,
  input  in_5,
  output out_6
);

  wire button_1_out, clock_1_out, n7_segment_decoder_1_a, n7_segment_decoder_1_b, n7_segment_decoder_1_c,
       n7_segment_decoder_1_d, n7_segment_decoder_1_e, n7_segment_decoder_1_f, n7_segment_decoder_1_g;
  wire [3:0] counter_1_q, random_1_out;
  wire [7:0] bit_extender_1_out;

  Button button_1 (.out(button_1_out));
  Clock clock_1 (.out(clock_1_out));
  Random #(.width(4)) random_1 (.clk(clock_1_out), .next(in_5), .out(random_1_out), .clr(button_1_out));
  assign bit_extender_1_out = {{4{1'b0}}, random_1_out};  // Bit_Extender bit_extender_1
  _7_segment_Decoder u_7_segment_decoder_1 (
    ._1(random_1_out[3]), ._2(random_1_out[2]), ._3(random_1_out[1]), ._4(random_1_out[0]),
    .a(n7_segment_decoder_1_a), .b(n7_segment_decoder_1_b), .c(n7_segment_decoder_1_c),
    .d(n7_segment_decoder_1_d), .e(n7_segment_decoder_1_e), .f(n7_segment_decoder_1_f),
    .g(n7_segment_decoder_1_g));
  Hex_Digit_Display hex_digit_display_1 (.value(bit_extender_1_out[7:4]), .dp(1'b0));
  Hex_Digit_Display hex_digit_display_2 (.value(bit_extender_1_out[3:0]), .dp(1'b0));
  _7_Segment_Display u_7_segment_display_1 (
    .g(n7_segment_decoder_1_g), .f(n7_segment_decoder_1_f), .a(n7_segment_decoder_1_a),
    .b(n7_segment_decoder_1_b), .e(n7_segment_decoder_1_e), .d(n7_segment_decoder_1_d),
    .c(n7_segment_decoder_1_c));  // open: dp
  LED led_1 (.in(out_6));
  LED led_2 (.in(in_1));
  Binary_Arcade binary_arcade_1 (
    .A(random_1_out[3]), .B(random_1_out[2]), .C(random_1_out[1]), .D(random_1_out[0]), ._8(in_4), ._4(in_3),
    ._2(in_2), ._1(in_1), .COUNT(out_6));
  LED led_3 (.in(in_2));
  LED led_4 (.in(in_3));
  LED led_5 (.in(in_4));
  Hex_Digit_Display hex_digit_display_3 (.value(counter_1_q));  // open: dp
  Counter #(.width(4), .max('h9)) counter_1 (
    .Q(counter_1_q), .clk(out_6), .clr(button_1_out));  // open: load, D, count, carry

  // Notes on the sheet:
  //   START BUTTON
  //   Dont forget to Enable it
  //   Reset Button 
  //   Clock
  //   4 bits Random Generator
  //   6. THE COUNTER IS RESET ONCE THE SCORE REACHES 10
  //   INSTRUTIONS
  //   1. PLEASE ENABLE THE GAME BY CLICKING ON THE ENABLE/START BUTTON
  //   2. ENABLE THE SIMULATION AND THEN ENABLE TICKS TO START THE GAME
  //   4. PLEASE INPUT THE 4 BIT BINARY EQUIVALENT IN THE GIVEN PLACE
  //   AR
  //   BiN       Y
  //   CA
  //   DE
  //   Bit Splitter
  //   3. A RANDOM NUMBER FROM 0-15 WILL BE GENERATED AND DISPLAYED ON THE HEX DISPLAY
  //   5. THE LED SHALL GLOW AND THE COUNTER WILL BE INCREMENTED IF THE ANSWER IS CORRECT
  //   GAME
  //   CIRCUIT
  //   Bit Extender
  //   Segment Decoder
  //   7 segment display
  //   Hex Decoder Display
  //   Ground
  //   8
  //   4 bits comparator
  //    Then answer
  //    is Right
  //   Enter the Binary Equvailent
  //   4
  //   IF this glows
  //   2
  //   Counter+1
  //   1
  //   USER INPUT
  //   Click to put (1,0)
  //   Score Display
endmodule

module C00 (
  input  in_1,
  input  in_2,
  input  in_3,
  input  in_4,
  output out_5
);

  wire and_1_out, and_2_out, and_3_out, and_4_out, and_5_out, and_6_out, and_7_out, not_1_out, not_2_out,
       not_3_out, not_4_out, not_5_out;

  not not_1 (not_1_out, in_4);
  not not_2 (not_2_out, in_3);
  not not_3 (not_3_out, in_2);
  not not_4 (not_4_out, in_1);
  not not_5 (not_5_out, in_3);
  and and_1 (and_1_out, in_3, not_1_out);
  and and_2 (and_2_out, in_2, in_3);
  and and_3 (and_3_out, not_3_out, not_1_out);
  and and_4 (and_4_out, not_4_out, in_2, in_4);
  and and_5 (and_5_out, not_4_out, in_3, in_4);
  and and_6 (and_6_out, in_1, not_5_out, not_1_out);
  and and_7 (and_7_out, not_2_out, in_1, not_3_out);
  or or_1 (out_5, and_1_out, and_2_out, and_3_out, and_7_out, and_4_out, and_5_out, and_6_out);

  // Notes on the sheet:
  //   0
endmodule

module C01 (
  input  _1,
  input  _2,
  input  _3,
  input  _4,
  output out_5
);

  wire and_1_out, and_2_out, and_3_out, and_4_out, and_5_out, not_1_out, not_2_out, not_3_out, not_4_out;

  not not_1 (not_1_out, _3);
  not not_2 (not_2_out, _4);
  not not_3 (not_3_out, _1);
  not not_4 (not_4_out, _2);
  and and_1 (and_1_out, not_3_out, not_4_out);
  and and_2 (and_2_out, not_3_out, not_1_out, not_2_out);
  and and_3 (and_3_out, not_3_out, _4, _3);
  and and_4 (and_4_out, not_1_out, _1, _4);
  and and_5 (and_5_out, not_4_out, not_2_out);
  or or_1 (out_5, and_1_out, and_2_out, and_3_out, and_4_out, and_5_out);

  // Notes on the sheet:
  //   K- Map of the B-light of the 7 segement Decoder Display
endmodule

module C02 (
  input  _1,
  input  _2,
  input  _3,
  input  _4,
  output out_5
);

  wire and_1_out, and_2_out, and_3_out, not_1_out, not_2_out, not_3_out, xor_1_out;

  not not_1 (not_1_out, _3);
  not not_2 (not_2_out, _4);
  not not_3 (not_3_out, _1);
  xor xor_1 (xor_1_out, _1, _2);
  and and_1 (and_1_out, not_1_out, _4);
  and and_2 (and_2_out, not_3_out, not_2_out, not_1_out);
  and and_3 (and_3_out, _4, _3, not_3_out);
  or or_1 (out_5, xor_1_out, and_2_out, and_3_out, and_1_out);

  // Notes on the sheet:
  //   K- Map of the C-light of the 7 segement Decoder Display
endmodule

module C03 (
  input  _1,
  input  _2,
  input  _3,
  input  _4,
  output out_5
);

  wire and_1_out, and_2_out, and_3_out, and_4_out, and_5_out, and_6_out, not_1_out, not_2_out, not_3_out,
       not_4_out;

  not not_1 (not_1_out, _1);
  not not_2 (not_2_out, _2);
  not not_3 (not_3_out, _3);
  not not_4 (not_4_out, _4);
  and and_1 (and_1_out, not_1_out, not_2_out, not_4_out);
  and and_2 (and_2_out, not_2_out, not_1_out, _3);
  and and_3 (and_3_out, _2, not_3_out, _4);
  and and_4 (and_4_out, _2, _3, not_4_out);
  and and_5 (and_5_out, _1, not_2_out, _4);
  and and_6 (and_6_out, _1, not_3_out);
  or or_1 (out_5, and_1_out, and_2_out, and_3_out, and_4_out, and_6_out, and_5_out);

  // Notes on the sheet:
  //   K- Map of the D-light of the 7 segement Decoder Display
endmodule

module C04 (
  input  _1,
  input  _2,
  input  _3,
  input  _4,
  output E
);

  wire and_1_out, and_2_out, and_3_out, and_4_out, not_1_out, not_2_out;

  not not_1 (not_1_out, _4);
  and and_1 (and_1_out, _1, _2);
  and and_2 (and_2_out, _3, not_1_out);
  not not_2 (not_2_out, _2);
  and and_3 (and_3_out, _1, _3);
  and and_4 (and_4_out, not_1_out, not_2_out);
  or or_1 (E, and_3_out, and_1_out, and_2_out, and_4_out);

  // Notes on the sheet:
  //   K- Map of the E-light of the 7 segement Decoder Display
endmodule

module C05 (
  input  _1,
  input  _2,
  input  _3,
  input  _4,
  output out_5
);

  wire and_1_out, and_2_out, and_3_out, and_4_out, and_5_out, not_1_out, not_2_out, not_3_out, not_4_out;

  not not_1 (not_1_out, _3);
  not not_2 (not_2_out, _4);
  not not_3 (not_3_out, _1);
  not not_4 (not_4_out, _2);
  and and_1 (and_1_out, not_2_out, not_1_out);
  and and_2 (and_2_out, not_4_out, _1);
  and and_3 (and_3_out, _1, _3);
  and and_4 (and_4_out, _2, _3, not_2_out);
  and and_5 (and_5_out, not_3_out, _2, not_1_out);
  or or_1 (out_5, and_1_out, and_2_out, and_3_out, and_4_out, and_5_out);

  // Notes on the sheet:
  //   K- Map of the F-light of the 7 segement Decoder Display
endmodule

module C06 (
  input  _1,
  input  _2,
  input  _3,
  input  _4,
  output G
);

  wire and_1_out, and_2_out, and_3_out, and_4_out, and_5_out, not_1_out, not_2_out, not_3_out;

  not not_1 (not_1_out, _3);
  not not_2 (not_2_out, _2);
  not not_3 (not_3_out, _1);
  and and_1 (and_1_out, _1, not_2_out);
  and and_2 (and_2_out, _4, not_1_out, _1);
  and and_3 (and_3_out, not_1_out, not_3_out, _2);
  and and_4 (and_4_out, not_3_out, not_2_out, _3);
  and and_5 (and_5_out, _1, _3);
  or or_1 (G, and_1_out, and_2_out, and_3_out, and_4_out, and_5_out);

  // Notes on the sheet:
  //   K- Map of the G-light of the 7 segement Decoder Display
endmodule

module Binary_Arcade (
  input  A,
  input  B,
  input  C,
  input  D,
  input  _8,
  input  _4,
  input  _2,
  input  _1,
  output COUNT
);

  wire and_1_out, and_2_out, xnor_1_out, xnor_2_out, xnor_3_out, xnor_4_out;

  LED led_1 (.in(_8));
  LED led_2 (.in(_4));
  LED led_3 (.in(_1));
  LED led_4 (.in(_2));
  xnor xnor_1 (xnor_1_out, _1, A);
  xnor xnor_2 (xnor_2_out, B, _2);
  xnor xnor_3 (xnor_3_out, C, _4);
  xnor xnor_4 (xnor_4_out, D, _8);
  and and_1 (and_1_out, xnor_1_out, xnor_2_out);
  and and_2 (and_2_out, xnor_3_out, xnor_4_out);
  and and_3 (COUNT, and_1_out, and_2_out);

  // Notes on the sheet:
  //   BINARY INPUT 
  //   k- map for 4 bits comparator to compare equivalency of the given input
endmodule

module _7_segment_Decoder (
  input  _1,
  input  _2,
  input  _3,
  input  _4,
  output a,
  output b,
  output c,
  output d,
  output e,
  output f,
  output g
);

  C01 c01_1 (._1(_1), ._2(_2), ._3(_3), ._4(_4), .out_5(b));
  C02 c02_1 (._1(_1), ._2(_2), ._3(_3), ._4(_4), .out_5(c));
  C03 c03_1 (._1(_1), ._2(_2), ._3(_3), ._4(_4), .out_5(d));
  C04 c04_1 (._1(_1), ._2(_2), ._3(_3), ._4(_4), .E(e));
  C05 c05_1 (._1(_1), ._2(_2), ._3(_3), ._4(_4), .out_5(f));
  C06 c06_1 (._1(_1), ._2(_2), ._3(_3), ._4(_4), .G(g));
  C00 c00_1 (.in_1(_1), .in_2(_2), .in_3(_3), .in_4(_4), .out_5(a));

  // Notes on the sheet:
  //   7 Segment Display Decoder Circuit
  //   a
  //   b
  //   c
  //   d
  //   e
  //   f
  //   g
  //   These chips contains the individual control of each lights in 7 segment display
endmodule
